# Fritzing sketch K3_dualswitch (saved by Fritzing 0.6.3b)
breadboards: 2

parts:
  Arduino1 = Arduino
  U1 = 74HC595 [package="DIP16 [THT]"]
  U2 = 74HC595 [package="DIP16 [THT]"]
  C1 = Ceramic Capacitor [capacitance=100nF package="100 mil [THT, multilayer]"]
  LED1 = LED - 5mm [color="Red (633nm)" package="5 mm [THT]"]
  LED2 = LED - 5mm [color="Red (633nm)" package="5 mm [THT]"]
  LED3 = LED - 5mm [color="Red (633nm)" package="5 mm [THT]"]
  LED4 = LED - 5mm [color="Red (633nm)" package="5 mm [THT]"]
  LED5 = LED - 5mm [color="Red (633nm)" package="5 mm [THT]"]
  LED6 = LED - 5mm [color="Red (633nm)" package="5 mm [THT]"]
  LED7 = LED - 5mm [color="Red (633nm)" package="5 mm [THT]"]
  LED8 = LED - 5mm [color="Red (633nm)" package="5 mm [THT]"]
  LED9 = LED - 5mm [color="Red (633nm)" package="5 mm [THT]"]
  LED10 = LED - 5mm [color="Red (633nm)" package="5 mm [THT]"]
  LED11 = LED - 5mm [color="Red (633nm)" package="5 mm [THT]"]
  LED12 = LED - 5mm [color="Red (633nm)" package="5 mm [THT]"]
  LED13 = LED - 5mm [color="Red (633nm)" package="5 mm [THT]"]
  LED14 = LED - 5mm [color="Red (633nm)" package="5 mm [THT]"]
  LED15 = LED - 5mm [color="Red (633nm)" package="5 mm [THT]"]
  LED16 = LED - 5mm [color="Red (633nm)" package="5 mm [THT]"]
  R1 = Resistor [tolerance=±5% resistance=220 package=THT]
  R2 = Resistor [tolerance=±5% resistance=220 package=THT]
  R3 = Resistor [tolerance=±5% resistance=220 package=THT]
  R4 = Resistor [tolerance=±5% resistance=220 package=THT]
  R5 = Resistor [tolerance=±5% resistance=220 package=THT]
  R6 = Resistor [tolerance=±5% resistance=220 package=THT]
  R7 = Resistor [tolerance=±5% resistance=220 package=THT]
  R8 = Resistor [tolerance=±5% resistance=220 package=THT]
  R9 = Resistor [tolerance=±5% resistance=220 package=THT]
  R10 = Resistor [tolerance=±5% resistance=220 package=THT]
  R11 = Resistor [tolerance=±5% resistance=220 package=THT]
  R12 = Resistor [tolerance=±5% resistance=220 package=THT]
  R13 = Resistor [tolerance=±5% resistance=220 package=THT]
  R14 = Resistor [tolerance=±5% resistance=220 package=THT]
  R15 = Resistor [tolerance=±5% resistance=220 package=THT]
  R16 = Resistor [tolerance=±5% resistance=220 package=THT]
  S1 = Toggle Switch [package=THT]
  S2 = Toggle Switch [package=THT]
  S3 = Toggle Switch [package=THT]
  S4 = Toggle Switch [package=THT]
  R17 = 10_k__Resistor
  R18 = 10_k__Resistor
  R19 = 10_k__Resistor
  R20 = 10_k__Resistor
  S5 = Pushbutton [package="[THT]"]
  S6 = Pushbutton [package="[THT]"]
  S7 = Pushbutton [package="[THT]"]
  S8 = Pushbutton [package="[THT]"]
  R21 = 47_k__Resistor
  R22 = 47_k__Resistor
  R23 = 47_k__Resistor
  R24 = 47_k__Resistor
  R25 = Resistor [tolerance=±5% resistance=220 package=THT]
  R26 = Resistor [tolerance=±5% resistance=220 package=THT]
  LED17 = LED - 5mm [color="Red (633nm)" package="5 mm [THT]"]
  LED18 = LED - 5mm [color="Red (633nm)" package="5 mm [THT]"]
  J1 = Piezo Speaker
  R27 = 2.2_k__Resistor

nets:
  GND: Arduino1.GND, U1.GND, U1.OE, U2.GND, U2.OE, C1.1, LED1.cathode, LED2.cathode, LED3.cathode, LED4.cathode, LED5.cathode, LED6.cathode, LED7.cathode, LED8.cathode, LED9.cathode, LED10.cathode, LED11.cathode, LED12.cathode, LED13.cathode, LED14.cathode, LED15.cathode, LED16.cathode, S1.L2, S2.L2, S3.L2, S4.L2, R21.connector0, R22.connector0, R23.connector0, R24.connector0, R25.Pin_0, R26.Pin_0, J1.pin1
  N1: Arduino1.D12, U1.SH_CP, U2.SH_CP
  N2: Arduino1.D11, U2.DS
  N3: Arduino1.D10, U1.ST_CP, U2.ST_CP, C1.0
  N4: Arduino1.D9, R27.connector1
  N5: Arduino1.D8, LED18.anode
  N6: Arduino1.D7, LED17.anode
  N7: Arduino1.D6, S8.Pin_1, S8.Pin_2, R24.connector1
  N8: Arduino1.D5, S4.COM, R20.connector0
  N9: Arduino1.D4, S3.COM, R19.connector0
  N10: Arduino1.D3, S2.COM, R18.connector0
  N11: Arduino1.D2, S1.COM, R17.connector0
  VCC: Arduino1.+5V, U1.MR, U1.VCC, U2.MR, U2.VCC, R17.connector1, R18.connector1, R19.connector1, R20.connector1, S5.Pin_3, S5.Pin_4, S6.Pin_3, S6.Pin_4, S7.Pin_3, S7.Pin_4, S8.Pin_3, S8.Pin_4
  N12: Arduino1.A0, S5.Pin_1, S5.Pin_2, R21.connector1
  N13: Arduino1.A2, S6.Pin_1, S6.Pin_2
  N14: Arduino1.A4, S7.Pin_1, S7.Pin_2, R23.connector1
  N15: U1.Q1, R10.Pin_1
  N16: U1.Q2, R11.Pin_1
  N17: U1.Q3, R12.Pin_1
  N18: U1.Q4, R13.Pin_1
  N19: U1.Q5, R14.Pin_1
  N20: U1.Q6, R15.Pin_1
  N21: U1.Q7, R16.Pin_1
  N22: U1.DS, U2.Q7'
  N23: U1.Q0, R9.Pin_1
  N24: U2.Q1, R2.Pin_1
  N25: U2.Q2, R3.Pin_1
  N26: U2.Q3, R4.Pin_1
  N27: U2.Q4, R5.Pin_1
  N28: U2.Q5, R6.Pin_1
  N29: U2.Q6, R7.Pin_1
  N30: U2.Q7, R8.Pin_1
  N31: U2.Q0, R1.Pin_1
  N32: LED1.anode, R1.Pin_0
  N33: LED2.anode, R2.Pin_0
  N34: LED3.anode, R3.Pin_0
  N35: LED4.anode, R4.Pin_0
  N36: LED5.anode, R5.Pin_0
  N37: LED6.anode, R6.Pin_0
  N38: LED7.anode, R7.Pin_0
  N39: LED8.anode, R8.Pin_0
  N40: LED9.anode, R9.Pin_0
  N41: LED10.anode, R10.Pin_0
  N42: LED11.anode, R11.Pin_0
  N43: LED12.anode, R12.Pin_0
  N44: LED13.anode, R13.Pin_0
  N45: LED14.anode, R14.Pin_0
  N46: LED15.anode, R15.Pin_0
  N47: LED16.anode, R16.Pin_0
  N48: R25.Pin_1, LED18.cathode
  N49: R26.Pin_1, LED17.cathode
  N50: J1.pin2, R27.connector0
